// Digital circuit 1_to_4_CLK.dig as structural Verilog
module _1_to_4_CLK (
  input  CLK,
  input  RST,
  output O1,
  output O2,
  output O3,
  output O4
);

  wire _74139_1_pin4, _74139_1_pin5, _74139_1_pin6, _74139_1_pin7, _74161_1_pin13, _74161_1_pin14;

  _74161 _74161_1 (
    .pin1(RST), .pin2(CLK), .pin3(1'b0), .pin4(1'b0), .pin5(1'b0), .pin6(1'b0), .pin7(1'b1), .pin8(1'b0),
    .pin9(1'b1), .pin10(1'b1), .pin13(_74161_1_pin13), .pin14(_74161_1_pin14), .pin16(1'b1));  // open: pin11, pin12, pin15
  not not_1 (O1, _74139_1_pin4);
  not not_2 (O2, _74139_1_pin5);
  not not_3 (O3, _74139_1_pin6);
  not not_4 (O4, _74139_1_pin7);
  _74139 _74139_1 (
    .pin1(1'b0), .pin2(_74161_1_pin14), .pin3(_74161_1_pin13), .pin4(_74139_1_pin4), .pin5(_74139_1_pin5),
    .pin6(_74139_1_pin6), .pin7(_74139_1_pin7), .pin8(1'b0), .pin13(1'b1), .pin14(1'b1), .pin15(1'b1),
    .pin16(1'b1));  // open: pin9, pin10, pin11, pin12
endmodule
