// Digital circuit CPUCore.dig as structural Verilog
module CPUCore (
  input  RST,
  input  CLK,
  output [15:0] ADDR,
  output [15:0] DATA,
  output RW
);

  wire _1_to_4_clk_1_o1, _1_to_4_clk_1_o2, _1_to_4_clk_1_o3, and_1_out, not_1_out, not_2_out, not_3_out,
       or_1_out;
  wire [15:0] pc_1_addrout;

  and and_1 (and_1_out, CLK, _1_to_4_clk_1_o1);
  _1_to_4_CLK _1_to_4_clk_1 (
    .CLK(CLK), .RST(RST), .O1(_1_to_4_clk_1_o1), .O2(_1_to_4_clk_1_o2), .O3(_1_to_4_clk_1_o3), .O4(RW));
  pc pc_1 (.CLK(and_1_out), .RESET(RST), .DIN(DATA), .ADDR(ADDR), .RW(RW), .ADDROUT(pc_1_addrout));
  or or_1 (or_1_out, _1_to_4_clk_1_o3, RW);
  not not_1 (not_1_out, _1_to_4_clk_1_o3);
  not not_2 (not_2_out, RW);
  not not_3 (not_3_out, RW);
  bus_driver_16 bus_driver_16_1 (.A(pc_1_addrout), .OE(or_1_out), .B(ADDR));
  latch_16 latch_16_1 (.OE(not_1_out), .IN(DATA), .LATCH(_1_to_4_clk_1_o1), .OUT(ADDR));
  latch_16 latch_16_2 (.OE(not_2_out), .IN(DATA), .LATCH(_1_to_4_clk_1_o2), .OUT(ADDR));
  latch_16 latch_16_3 (.OE(not_3_out), .IN(DATA), .LATCH(_1_to_4_clk_1_o3), .OUT(DATA));

  // Notes on the sheet:
  //   Source address
  //   Destination address
  //   Read data
endmodule
