// Digital circuit GPIO.dig as structural Verilog
module GPIO (
  input  [15:0] Addr,
  input  [15:0] data,
  input  RW,
  input  CLK,
  output [15:0] GPIO
);

  wire and_1_out, comparator_1_eq, not_1_out;

  not not_1 (not_1_out, CLK);
  Comparator #(.Bits(16)) comparator_1 (.a(Addr), .b(16'hfe00), .eq(comparator_1_eq));  // open: gt, lt
  and and_1 (and_1_out, comparator_1_eq, RW, not_1_out);
  reg_16 reg_16_1 (.OE(1'b0), .IN(data), .CLK(and_1_out), .OUT(GPIO));
endmodule
