// Digital circuit MOVPuter.dig as structural Verilog
module MOVPuter (
  input  clk,
  input  RST,
  output [15:0] DATA,
  output [15:0] GPIO
);

  wire cpucore_1_rw, nor_1_out, nor_2_out, not_1_out;
  wire [11:0] cpucore_1_addr, register_1_q;
  wire [15:12] cpucore_1_addr_2;

  CPUCore cpucore_1 (.RST(RST), .CLK(clk), .ADDR({cpucore_1_addr_2, cpucore_1_addr}), .DATA(DATA), .RW(cpucore_1_rw));
  not not_1 (not_1_out, cpucore_1_addr_2[15]);
  nor nor_1 (nor_1_out, cpucore_1_addr_2[14], cpucore_1_addr_2[15]);
  nor nor_2 (nor_2_out, cpucore_1_addr_2[14], not_1_out);
  Register #(.Bits(12)) register_1 (.D(cpucore_1_addr), .C(clk), .en(1'b1), .Q(register_1_q));
  EEPROM #(.AddrBits(12), .Bits(16)) eeprom_1 (.A(cpucore_1_addr), .CS(nor_1_out), .WE(1'b0), .OE(nor_1_out), .D(DATA));
  RAMSinglePortSel #(.AddrBits(12), .Bits(16)) ramsingleportsel_1 (
    .A(register_1_q), .CS(nor_2_out), .WE(cpucore_1_rw), .OE(nor_2_out), .D(DATA));
  GPIO gpio_1 (.Addr({cpucore_1_addr_2, cpucore_1_addr}), .data(DATA), .RW(cpucore_1_rw), .CLK(clk), .GPIO(GPIO));
  comp comp_1 (.Addr({cpucore_1_addr_2, cpucore_1_addr}), .data(DATA), .RW(cpucore_1_rw), .CLK(clk));
  alu alu_1 (.Addr({cpucore_1_addr_2, cpucore_1_addr}), .data(DATA), .RW(cpucore_1_rw), .CLK(clk));  // open: Carry

  // Notes on the sheet:
  //   clk: Hz: 50
  //   ROM: 0x0000 to 0x8000
  //   RAM 0x8000 to 0xC000
  //   Periph: 0xC000 to 0xFFFE 
  //   ALU = 0xc000
  //   Comp = 0xC100
  //   GPIO = 0xFE00
  //   PC: 0xFFFF
  //   contents of eeprom_1 (hex, n*v repeats v):
  //   64,c102,65,c101,66,c100,67,8001,8000,c000,8001,c020,8001,8000,c012,8001,8001,fe00,
  //   8002,c000,67,c020,c012,8002,8002,c103,c100,ffff,65,ffff,0,0,0,0,0,0,0,0,0,0,0,0,0,
  //   0,0,0,0,0,0,0,0,0,0,0,0,0,0,0,0,0,0,0,0,0,0,0,0,0,0,0,0,0,0,0,0,0,0,0,0,0,0,0,0,0,
  //   0,0,0,0,0,0,0,0,0,0,0,0,0,0,0,0,a,1c,8,1
endmodule
