// Digital circuit alu.dig as structural Verilog
module alu (
  input  [15:0] Addr,
  input  [15:0] data,
  input  RW,
  input  CLK,
  output Carry
);

  wire alu_slice_1_carry_out, alu_slice_2_carry_out, alu_slice_3_carry_out, and_1_out, and_2_out, and_3_out,
       comparator_1_eq, not_1_out, not_2_out, not_3_out, not_4_out;
  wire [15:0] alu_slice_1_f, reg_16_1_out, reg_16_2_out;

  Comparator #(.Bits(10)) comparator_1 (.a(Addr[15:6]), .b(10'h300), .eq(comparator_1_eq));  // open: gt, lt
  not not_1 (not_1_out, CLK);
  not not_2 (not_2_out, Addr[5]);
  not not_3 (not_3_out, RW);
  reg_16 reg_16_1 (.OE(1'b0), .IN(data), .CLK(and_1_out), .OUT(reg_16_1_out));
  reg_16 reg_16_2 (.OE(1'b0), .IN(data), .CLK(and_2_out), .OUT(reg_16_2_out));
  and and_1 (and_1_out, comparator_1_eq, RW, Addr[5], not_1_out);
  and and_2 (and_2_out, comparator_1_eq, RW, not_2_out, not_1_out);
  and and_3 (and_3_out, comparator_1_eq, not_3_out);
  not not_4 (not_4_out, and_3_out);
  alu_slice alu_slice_1 (
    .Carry_in(1'b1), .Opcode(Addr[4:0]), .B(reg_16_1_out[3:0]), .A(reg_16_2_out[3:0]),
    .Carry_out(alu_slice_1_carry_out), .F(alu_slice_1_f[3:0]));
  alu_slice alu_slice_2 (
    .Carry_in(alu_slice_1_carry_out), .Opcode(Addr[4:0]), .B(reg_16_1_out[7:4]), .A(reg_16_2_out[7:4]),
    .Carry_out(alu_slice_2_carry_out), .F(alu_slice_1_f[7:4]));
  alu_slice alu_slice_3 (
    .Carry_in(alu_slice_2_carry_out), .Opcode(Addr[4:0]), .B(reg_16_1_out[11:8]), .A(reg_16_2_out[11:8]),
    .Carry_out(alu_slice_3_carry_out), .F(alu_slice_1_f[11:8]));
  alu_slice alu_slice_4 (
    .Carry_in(alu_slice_3_carry_out), .Opcode(Addr[4:0]), .B(reg_16_1_out[15:12]), .A(reg_16_2_out[15:12]),
    .Carry_out(Carry), .F(alu_slice_1_f[15:12]));
  bus_driver_16 bus_driver_16_1 (.A(alu_slice_1_f), .OE(not_4_out), .B(data));
endmodule
