// Digital circuit alu_slice.dig as structural Verilog
module alu_slice (
  input  Carry_in,
  input  [4:0] Opcode,
  input  [3:0] B,
  input  [3:0] A,
  output Carry_out,
  output [3:0] F
);

  _74181 _74181_1 (
    .pin1(B[0]), .pin2(A[0]), .pin3(Opcode[1]), .pin4(Opcode[2]), .pin5(Opcode[3]), .pin6(Opcode[4]),
    .pin7(Carry_in), .pin8(Opcode[0]), .pin9(F[0]), .pin10(F[1]), .pin11(F[2]), .pin12(1'b0));  // open: pin13, pin14, pin15, pin16, pin17, pin18, pin19, pin20, pin21, pin22, pin23, pin24
endmodule
