// Digital circuit bus_driver_16.dig as structural Verilog
module bus_driver_16 (
  input  [15:0] A,
  input  OE,
  output [15:0] B
);

  _74245 _74245_1 (
    .pin1(1'b1), .pin2(A[0]), .pin3(A[1]), .pin4(A[2]), .pin5(A[3]), .pin6(A[4]), .pin7(A[5]), .pin8(A[6]),
    .pin9(A[7]), .pin10(1'b0), .pin11(B[7]), .pin12(B[6]), .pin13(B[5]), .pin14(B[4]), .pin15(B[3]),
    .pin16(B[2]), .pin17(B[1]), .pin18(B[0]), .pin19(OE), .pin20(1'b1));
  _74245 _74245_2 (
    .pin1(1'b1), .pin2(A[8]), .pin3(A[9]), .pin4(A[10]), .pin5(A[11]), .pin6(A[12]), .pin7(A[13]),
    .pin8(A[14]), .pin9(A[15]), .pin10(1'b0), .pin11(B[15]), .pin12(B[14]), .pin13(B[13]), .pin14(B[12]),
    .pin15(B[11]), .pin16(B[10]), .pin17(B[9]), .pin18(B[8]), .pin19(OE), .pin20(1'b1));
endmodule
