// Digital circuit comp.dig as structural Verilog
module comp (
  input  [15:0] Addr,
  input  [15:0] data,
  input  RW,
  input  CLK
);

  wire and_1_out, and_2_out, and_3_out, and_4_out, comparator_1_eq, comparator_2_eq, decoder_1_out_0,
       decoder_1_out_1, decoder_1_out_2, decoder_1_out_3, nand_1_out, nand_2_out, not_1_out, not_2_out,
       not_3_out;
  wire [15:0] reg_16_3_out, reg_16_4_out;

  not not_1 (not_1_out, CLK);
  Decoder #(.Selector_Bits(2)) decoder_1 (
    .sel(Addr[1:0]), .out_0(decoder_1_out_0), .out_1(decoder_1_out_1), .out_2(decoder_1_out_2),
    .out_3(decoder_1_out_3));
  Comparator #(.Bits(13)) comparator_1 (.a(Addr[15:3]), .b(13'h1820), .eq(comparator_1_eq));  // open: gt, lt
  and and_1 (and_1_out, decoder_1_out_0, comparator_1_eq, not_1_out);
  and and_2 (and_2_out, decoder_1_out_1, comparator_1_eq, not_1_out);
  and and_3 (and_3_out, decoder_1_out_2, comparator_1_eq, not_1_out);
  and and_4 (and_4_out, decoder_1_out_3, comparator_1_eq, not_1_out);
  reg_16 reg_16_1 (.OE(nand_1_out), .IN(data), .CLK(and_1_out), .OUT(data));
  reg_16 reg_16_2 (.OE(nand_2_out), .IN(data), .CLK(and_2_out), .OUT(data));
  reg_16 reg_16_3 (.OE(1'b0), .IN(data), .CLK(and_3_out), .OUT(reg_16_3_out));
  reg_16 reg_16_4 (.OE(1'b0), .IN(data), .CLK(and_4_out), .OUT(reg_16_4_out));
  Comparator #(.Bits(16)) comparator_2 (.a(reg_16_3_out), .b(reg_16_4_out), .eq(comparator_2_eq));  // open: gt, lt
  not not_2 (not_2_out, RW);
  nand nand_1 (nand_1_out, not_3_out, not_2_out, comparator_1_eq);
  nand nand_2 (nand_2_out, comparator_2_eq, not_2_out, comparator_1_eq);
  not not_3 (not_3_out, comparator_2_eq);
endmodule
