// Digital circuit latch_16.dig as structural Verilog
module latch_16 (
  input  OE,
  input  [15:0] IN,
  input  LATCH,
  output [15:0] OUT
);

  _74573 _74573_1 (
    .pin1(OE), .pin2(IN[0]), .pin3(IN[1]), .pin4(IN[2]), .pin5(IN[3]), .pin6(IN[4]), .pin7(IN[5]),
    .pin8(IN[6]), .pin9(IN[7]), .pin10(1'b0), .pin11(LATCH), .pin12(OUT[7]), .pin13(OUT[6]), .pin14(OUT[5]),
    .pin15(OUT[4]), .pin16(OUT[3]), .pin17(OUT[2]), .pin18(OUT[1]), .pin19(OUT[0]), .pin20(1'b1));
  _74573 _74573_2 (
    .pin1(OE), .pin2(IN[8]), .pin3(IN[9]), .pin4(IN[10]), .pin5(IN[11]), .pin6(IN[12]), .pin7(IN[13]),
    .pin8(IN[14]), .pin9(IN[15]), .pin10(1'b0), .pin11(LATCH), .pin12(OUT[15]), .pin13(OUT[14]),
    .pin14(OUT[13]), .pin15(OUT[12]), .pin16(OUT[11]), .pin17(OUT[10]), .pin18(OUT[9]), .pin19(OUT[8]),
    .pin20(1'b1));
endmodule
