// Digital circuit pc.dig as structural Verilog
module pc (
  input  CLK,
  input  RESET,
  input  [15:0] DIN,
  input  [15:0] ADDR,
  input  RW,
  output [15:0] ADDROUT
);

  wire _74161_1_pin15, _74161_2_pin15, _74161_3_pin15, _74161_4_pin15, and_1_out, comparator_1_eq, not_1_out;

  Comparator #(.Bits(16)) comparator_1 (.a(ADDR), .b({16{1'b1}}), .eq(comparator_1_eq));  // open: gt, lt
  and and_1 (and_1_out, comparator_1_eq, RW);
  not not_1 (not_1_out, and_1_out);
  _74161 _74161_1 (
    .pin1(RESET), .pin2(CLK), .pin3(DIN[0]), .pin4(DIN[1]), .pin5(DIN[2]), .pin6(DIN[3]), .pin7(1'b1),
    .pin8(1'b0), .pin9(not_1_out), .pin10(1'b1), .pin11(ADDROUT[3]), .pin12(ADDROUT[2]), .pin13(ADDROUT[1]),
    .pin14(ADDROUT[0]), .pin15(_74161_1_pin15), .pin16(1'b1));
  _74161 _74161_2 (
    .pin1(RESET), .pin2(CLK), .pin3(DIN[4]), .pin4(DIN[5]), .pin5(DIN[6]), .pin6(DIN[7]), .pin7(1'b1),
    .pin8(1'b0), .pin9(not_1_out), .pin10(_74161_1_pin15), .pin11(ADDROUT[7]), .pin12(ADDROUT[6]),
    .pin13(ADDROUT[5]), .pin14(ADDROUT[4]), .pin15(_74161_2_pin15), .pin16(1'b1));
  _74161 _74161_3 (
    .pin1(RESET), .pin2(CLK), .pin3(DIN[8]), .pin4(DIN[9]), .pin5(DIN[10]), .pin6(DIN[11]), .pin7(1'b1),
    .pin8(1'b0), .pin9(not_1_out), .pin10(_74161_2_pin15), .pin11(ADDROUT[11]), .pin12(ADDROUT[10]),
    .pin13(ADDROUT[9]), .pin14(ADDROUT[8]), .pin15(_74161_3_pin15), .pin16(1'b1));
  _74161 _74161_4 (
    .pin1(RESET), .pin2(CLK), .pin3(DIN[12]), .pin4(DIN[13]), .pin5(DIN[14]), .pin6(DIN[15]), .pin7(1'b1),
    .pin8(1'b0), .pin9(not_1_out), .pin10(_74161_3_pin15), .pin11(ADDROUT[15]), .pin12(ADDROUT[14]),
    .pin13(ADDROUT[13]), .pin14(ADDROUT[12]), .pin15(_74161_4_pin15), .pin16(1'b1));
  LED led_1 (.in(_74161_4_pin15));
endmodule
