// Digital circuit reg_16.dig as structural Verilog
module reg_16 (
  input  OE,
  input  [15:0] IN,
  input  CLK,
  output [15:0] OUT
);

  _74374 _74374_1 (
    .pin1(OE), .pin2(OUT[0]), .pin3(IN[0]), .pin4(IN[1]), .pin5(OUT[1]), .pin6(OUT[2]), .pin7(IN[2]),
    .pin8(IN[3]), .pin9(OUT[3]), .pin10(1'b0), .pin11(CLK), .pin12(OUT[4]), .pin13(IN[4]), .pin14(IN[5]),
    .pin15(OUT[5]), .pin16(OUT[6]), .pin17(IN[6]), .pin18(IN[7]), .pin19(OUT[7]), .pin20(1'b1));
  _74374 _74374_2 (
    .pin1(OE), .pin2(OUT[8]), .pin3(IN[8]), .pin4(IN[9]), .pin5(OUT[9]), .pin6(OUT[10]), .pin7(IN[10]),
    .pin8(IN[11]), .pin9(OUT[11]), .pin10(1'b0), .pin11(CLK), .pin12(OUT[12]), .pin13(IN[12]),
    .pin14(IN[13]), .pin15(OUT[13]), .pin16(OUT[14]), .pin17(IN[14]), .pin18(IN[15]), .pin19(OUT[15]),
    .pin20(1'b1));
endmodule
